// Logisim project Project smart street light updated.circ as structural Verilog: 1 circuit, main circuit main
module main (
  input  Motion,
  input  Day_Night_Time,
  input  Light,
  output out_4
);

  wire or_1_out;

  or or_1 (or_1_out, Motion, Day_Night_Time);
  and and_1 (out_4, or_1_out, Light);
endmodule
